// Logisim project Digit Display.circ as structural Verilog: 1 circuit, main circuit main
module main (
  input  [7:0] in_1
);

  wire and_1_out, and_2_out, and_3_out, and_4_out, and_5_out, and_6_out, and_7_out, and_8_out, and_9_out,
       and_10_out, and_11_out, and_12_out, and_13_out, and_14_out, and_15_out, not_1_out, not_2_out,
       not_3_out, not_4_out, not_5_out, not_6_out, not_7_out, not_8_out, not_9_out, not_10_out, not_11_out,
       not_12_out, not_13_out, not_14_out, not_15_out, not_16_out, not_17_out, not_18_out, not_19_out,
       not_20_out, not_21_out, not_22_out, not_23_out, not_24_out, not_25_out, not_26_out, not_27_out,
       not_28_out, not_29_out, not_30_out, not_31_out, not_32_out, not_33_out, not_34_out, not_35_out,
       not_36_out, not_37_out, not_38_out, not_39_out, not_40_out, not_41_out, not_42_out, not_43_out,
       or_1_out, or_2_out, or_3_out, or_4_out, or_5_out, or_6_out;

  not not_1 (not_1_out, in_1[0]);
  not not_2 (not_2_out, in_1[1]);
  not not_3 (not_3_out, in_1[3]);
  not not_4 (not_4_out, in_1[1]);
  not not_5 (not_5_out, in_1[2]);
  not not_6 (not_6_out, in_1[3]);
  not not_7 (not_7_out, in_1[0]);
  not not_8 (not_8_out, in_1[3]);
  not not_9 (not_9_out, in_1[1]);
  not not_10 (not_10_out, in_1[3]);
  not not_11 (not_11_out, in_1[0]);
  not not_12 (not_12_out, in_1[2]);
  not not_13 (not_13_out, in_1[3]);
  not not_14 (not_14_out, in_1[1]);
  not not_15 (not_15_out, in_1[2]);
  not not_16 (not_16_out, in_1[3]);
  not not_17 (not_17_out, in_1[0]);
  not not_18 (not_18_out, in_1[1]);
  not not_19 (not_19_out, in_1[3]);
  not not_20 (not_20_out, in_1[3]);
  not not_21 (not_21_out, in_1[0]);
  and and_1 (and_1_out, not_21_out, not_22_out, not_23_out);
  not not_22 (not_22_out, in_1[2]);
  not not_23 (not_23_out, in_1[3]);
  not not_24 (not_24_out, in_1[0]);
  not not_25 (not_25_out, in_1[3]);
  not not_26 (not_26_out, in_1[0]);
  not not_27 (not_27_out, in_1[1]);
  not not_28 (not_28_out, in_1[2]);
  and and_2 (and_2_out, not_1_out, not_2_out, in_1[2], not_3_out);
  and and_3 (and_3_out, in_1[0], not_4_out, not_5_out, not_6_out);
  and and_4 (and_4_out, not_7_out, in_1[1], in_1[2], not_8_out);
  or or_1 (or_1_out, and_4_out, and_5_out);
  and and_5 (and_5_out, in_1[0], not_9_out, in_1[2], not_10_out);
  not not_29 (not_29_out, and_6_out);
  and and_6 (and_6_out, not_11_out, in_1[1], not_12_out, not_13_out);
  and and_7 (and_7_out, in_1[0], not_14_out, not_15_out, not_16_out);
  or or_2 (or_2_out, and_7_out, and_8_out, and_9_out);
  and and_8 (and_8_out, not_17_out, not_18_out, in_1[2], not_19_out);
  and and_9 (and_9_out, in_1[0], in_1[1], in_1[2], not_20_out);
  or or_3 (or_3_out, and_1_out, and_10_out, and_11_out);
  and and_10 (and_10_out, not_24_out, in_1[1], in_1[2], not_25_out);
  and and_11 (and_11_out, not_26_out, not_27_out, not_28_out, in_1[3]);
  or or_4 (or_4_out, and_2_out, and_3_out);
  not not_30 (not_30_out, or_4_out);
  not not_31 (not_31_out, or_1_out);
  not not_32 (not_32_out, or_2_out);
  not not_33 (not_33_out, or_5_out);
  or or_5 (or_5_out, and_12_out, and_13_out);
  and and_12 (and_12_out, in_1[0], not_35_out, not_36_out, not_34_out);
  not not_34 (not_34_out, in_1[3]);
  not not_35 (not_35_out, in_1[1]);
  not not_36 (not_36_out, in_1[2]);
  and and_13 (and_13_out, in_1[1], not_38_out, not_37_out);
  not not_37 (not_37_out, in_1[3]);
  not not_38 (not_38_out, in_1[2]);
  not not_39 (not_39_out, in_1[1]);
  not not_40 (not_40_out, or_6_out);
  or or_6 (or_6_out, and_15_out, and_14_out);
  and and_14 (and_14_out, in_1[0], in_1[1], in_1[2], not_43_out);
  and and_15 (and_15_out, not_39_out, not_42_out, not_41_out);
  not not_41 (not_41_out, in_1[3]);
  not not_42 (not_42_out, in_1[2]);
  not not_43 (not_43_out, in_1[3]);
  _7_Segment_Display u_7_segment_display_1 (
    .g(not_40_out), .f(not_33_out), .a(not_30_out), .b(not_31_out), .e(or_3_out), .d(not_32_out),
    .c(not_29_out));  // open: dp
endmodule
