// Logisim project PCandIR.circ as structural Verilog: 3 circuits, main circuit main
module main (
  input  Status_Bit,
  input  in_2,
  input  Jmp_status,
  input  in_4,
  input  in_5,
  input  in_6,
  input  in_7
);

  wire and_1_out, and_2_out, and_3_out, and_4_out, and_5_out, and_6_out, and_7_out, and_8_out, and_9_out,
       and_10_out, and_11_out, and_12_out, and_13_out, and_14_out, and_15_out, and_16_out, and_17_out,
       clock_1_out, j_k_ff_1_qn, j_k_ff_2_qn, j_k_ff_3_qn, j_k_ff_4_qn, not_1_out, not_2_out, not_3_out,
       not_4_out, not_5_out, not_6_out, not_7_out, not_8_out, not_9_out, not_10_out, not_11_out, not_12_out,
       not_13_out, not_14_out, not_15_out, not_16_out, not_17_out, not_18_out, not_19_out, not_20_out,
       not_21_out, not_22_out, not_23_out, not_24_out, not_25_out, not_26_out, not_27_out, not_28_out,
       not_29_out, not_30_out, not_31_out, not_32_out, not_33_out;
  wire [7:0] register_1_q, register_2_q, register_3_q, register_4_q, register_5_q, register_6_q,
       register_7_q, register_8_q, register_9_q, register_10_q, register_11_q, register_12_q, register_13_q,
       register_14_q, register_15_q, register_16_q;

  Clock clock_1 (.out(clock_1_out));
  and and_1 (and_1_out, clock_1_out, not_1_out);
  not not_1 (not_1_out, in_4);
  J_K_Flip_Flop j_k_ff_1 (
    .J(in_2), .clk(and_1_out), .K(in_2), .Qn(j_k_ff_1_qn), .reset(Jmp_status));  // open: Q, preset, en
  not not_2 (not_2_out, j_k_ff_1_qn);
  not not_3 (not_3_out, j_k_ff_1_qn);
  not not_4 (not_4_out, j_k_ff_1_qn);
  not not_5 (not_5_out, j_k_ff_1_qn);
  not not_6 (not_6_out, j_k_ff_1_qn);
  not not_7 (not_7_out, j_k_ff_1_qn);
  not not_8 (not_8_out, j_k_ff_1_qn);
  not not_9 (not_9_out, j_k_ff_1_qn);
  not not_10 (not_10_out, j_k_ff_2_qn);
  not not_11 (not_11_out, j_k_ff_2_qn);
  not not_12 (not_12_out, j_k_ff_2_qn);
  not not_13 (not_13_out, j_k_ff_2_qn);
  not not_14 (not_14_out, j_k_ff_2_qn);
  not not_15 (not_15_out, j_k_ff_2_qn);
  not not_16 (not_16_out, j_k_ff_2_qn);
  not not_17 (not_17_out, j_k_ff_2_qn);
  J_K_Flip_Flop j_k_ff_2 (
    .J(in_2), .clk(j_k_ff_1_qn), .K(in_2), .Qn(j_k_ff_2_qn), .reset(Jmp_status));  // open: Q, preset, en
  not not_18 (not_18_out, j_k_ff_3_qn);
  not not_19 (not_19_out, j_k_ff_3_qn);
  not not_20 (not_20_out, j_k_ff_3_qn);
  not not_21 (not_21_out, j_k_ff_3_qn);
  not not_22 (not_22_out, j_k_ff_3_qn);
  not not_23 (not_23_out, j_k_ff_3_qn);
  not not_24 (not_24_out, j_k_ff_3_qn);
  not not_25 (not_25_out, j_k_ff_3_qn);
  not not_26 (not_26_out, j_k_ff_4_qn);
  not not_27 (not_27_out, j_k_ff_4_qn);
  not not_28 (not_28_out, j_k_ff_4_qn);
  not not_29 (not_29_out, j_k_ff_4_qn);
  not not_30 (not_30_out, j_k_ff_4_qn);
  not not_31 (not_31_out, j_k_ff_4_qn);
  not not_32 (not_32_out, j_k_ff_4_qn);
  not not_33 (not_33_out, j_k_ff_4_qn);
  J_K_Flip_Flop j_k_ff_3 (
    .J(in_2), .clk(j_k_ff_2_qn), .K(in_2), .Qn(j_k_ff_3_qn), .reset(Jmp_status));  // open: Q, preset, en
  and and_2 (and_2_out, Status_Bit, not_2_out, not_10_out, not_18_out, not_26_out);
  and and_3 (and_3_out, Status_Bit, j_k_ff_1_qn, not_11_out, not_19_out, not_27_out);
  and and_4 (and_4_out, Status_Bit, not_3_out, j_k_ff_2_qn, not_20_out, not_28_out);
  and and_5 (and_5_out, Status_Bit, j_k_ff_1_qn, j_k_ff_2_qn, not_21_out, not_29_out);
  and and_6 (and_6_out, Status_Bit, not_4_out, not_12_out, j_k_ff_3_qn, not_30_out);
  and and_7 (and_7_out, Status_Bit, j_k_ff_1_qn, not_13_out, j_k_ff_3_qn, not_31_out);
  and and_8 (and_8_out, Status_Bit, not_5_out, j_k_ff_2_qn, j_k_ff_3_qn, not_32_out);
  and and_9 (and_9_out, Status_Bit, j_k_ff_1_qn, j_k_ff_2_qn, j_k_ff_3_qn, not_33_out);
  and and_10 (and_10_out, Status_Bit, not_6_out, not_14_out, not_22_out, j_k_ff_4_qn);
  and and_11 (and_11_out, Status_Bit, j_k_ff_1_qn, not_15_out, not_23_out, j_k_ff_4_qn);
  and and_12 (and_12_out, Status_Bit, not_7_out, j_k_ff_2_qn, not_24_out, j_k_ff_4_qn);
  and and_13 (and_13_out, Status_Bit, j_k_ff_1_qn, j_k_ff_2_qn, not_25_out, j_k_ff_4_qn);
  and and_14 (and_14_out, Status_Bit, not_8_out, not_16_out, j_k_ff_3_qn, j_k_ff_4_qn);
  and and_15 (and_15_out, Status_Bit, j_k_ff_1_qn, not_17_out, j_k_ff_3_qn, j_k_ff_4_qn);
  and and_16 (and_16_out, Status_Bit, not_9_out, j_k_ff_2_qn, j_k_ff_3_qn, j_k_ff_4_qn);
  and and_17 (and_17_out, Status_Bit, j_k_ff_1_qn, j_k_ff_2_qn, j_k_ff_3_qn, j_k_ff_4_qn);
  J_K_Flip_Flop j_k_ff_4 (
    .J(in_2), .clk(j_k_ff_3_qn), .K(in_2), .Qn(j_k_ff_4_qn), .reset(Jmp_status));  // open: Q, preset, en
  Register register_1 (.Q(register_1_q), .clk(and_2_out));  // open: D, en, clr
  Register register_2 (.Q(register_2_q), .clk(and_3_out));  // open: D, en, clr
  Register register_3 (.Q(register_3_q), .clk(and_4_out));  // open: D, en, clr
  Register register_4 (.Q(register_4_q), .clk(and_5_out));  // open: D, en, clr
  Register register_5 (.Q(register_5_q), .clk(and_6_out));  // open: D, en, clr
  Register register_6 (.Q(register_6_q), .clk(and_7_out));  // open: D, en, clr
  Register register_7 (.Q(register_7_q), .clk(and_8_out));  // open: D, en, clr
  Register register_8 (.Q(register_8_q), .clk(and_9_out));  // open: D, en, clr
  Register register_9 (.Q(register_9_q), .clk(and_10_out));  // open: D, en, clr
  Register register_10 (.Q(register_10_q), .clk(and_11_out));  // open: D, en, clr
  Register register_11 (.Q(register_11_q), .clk(and_12_out));  // open: D, en, clr
  Register register_12 (.Q(register_12_q), .clk(and_13_out));  // open: D, en, clr
  Register register_13 (.Q(register_13_q), .clk(and_14_out));  // open: D, en, clr
  Register register_14 (.Q(register_14_q), .clk(and_15_out));  // open: D, en, clr
  Register register_15 (.Q(register_15_q), .clk(and_16_out));  // open: D, en, clr
  Register register_16 (.Q(register_16_q), .clk(and_17_out));  // open: D, en, clr
  Register register_17 (.D(register_16_q), .en(and_17_out), .clk(and_17_out));  // open: Q, clr

  // Notes on the sheet:
  //   Power, must always be one
  //   Instruction 15
  //   Instruction 14
  //   Instruction 13
  //   Instruction 12
  //   Instruction 11
  //   Instruction 10
  //   Instruction 9
  //   Instruction 8
  //   Instruction 7
  //   Instruction 6
  //   Instruction 5
  //   Instruction 4
  //   Instruction 3
  //   Instruction 2
  //   Instruction 1
  //   Instruction 0 
  //   and clock them, all the clocks need to go off at the same time after the jmp status
  //   Goes on. Then tick the ones that should be on, using and gates.
endmodule

module Half_Byte (
  input  in_1,
  input  in_2,
  input  in_3,
  output out_4,
  output out_5,
  output out_6,
  output out_7
);

  wire and_1_out, and_2_out, and_3_out, and_4_out, and_5_out, not_1_out, not_2_out, not_3_out, not_4_out,
       s_r_ff_1_q, s_r_ff_2_q, s_r_ff_3_q, s_r_ff_4_q, undriven, undriven_2, undriven_3, undriven_4;

  and and_1 (and_1_out, in_1, in_2);
  not not_1 (not_1_out, undriven);
  not not_2 (not_2_out, undriven_3);
  not not_3 (not_3_out, undriven_4);
  not not_4 (not_4_out, undriven_2);
  S_R_Flip_Flop s_r_ff_1 (.S(undriven), .clk(and_1_out), .R(and_2_out), .Q(s_r_ff_1_q));  // open: Qn, preset, reset, en
  and and_2 (and_2_out, not_1_out, in_3);
  S_R_Flip_Flop s_r_ff_2 (
    .S(undriven_3), .clk(and_1_out), .R(and_3_out), .Q(s_r_ff_2_q));  // open: Qn, preset, reset, en
  and and_3 (and_3_out, not_2_out, in_3);
  S_R_Flip_Flop s_r_ff_3 (
    .S(undriven_4), .clk(and_1_out), .R(and_4_out), .Q(s_r_ff_3_q));  // open: Qn, preset, reset, en
  and and_4 (and_4_out, not_3_out, in_3);
  S_R_Flip_Flop s_r_ff_4 (
    .S(undriven_2), .clk(and_1_out), .R(and_5_out), .Q(s_r_ff_4_q));  // open: Qn, preset, reset, en
  buf and_5 (and_5_out, not_4_out);  // AND_Gate
  and and_6 (out_4, in_2, s_r_ff_1_q);
  and and_7 (out_5, in_2, s_r_ff_2_q);
  and and_8 (out_6, in_2, s_r_ff_3_q);
  and and_9 (out_7, in_2, s_r_ff_4_q);

  // Notes on the sheet:
  //   Byte of Memory #2
endmodule

module Full_Byte (
  input  in_1,
  input  in_2,
  input  in_3,
  input  in_4,
  input  in_5,
  input  in_6,
  input  in_7,
  input  in_8,
  input  in_9,
  input  in_10,
  input  in_11,
  output out_12,
  output out_13,
  output out_14,
  output out_15,
  output out_16,
  output out_17,
  output out_18,
  output out_19
);

  wire and_1_out, and_2_out, and_3_out, and_4_out, and_5_out, and_6_out, and_7_out, and_8_out, and_9_out,
       not_1_out, not_2_out, not_3_out, not_4_out, not_5_out, not_6_out, not_7_out, not_8_out, s_r_ff_1_q,
       s_r_ff_2_q, s_r_ff_3_q, s_r_ff_4_q, s_r_ff_5_q, s_r_ff_6_q, s_r_ff_7_q, s_r_ff_8_q;

  and and_1 (and_1_out, in_1, in_2);
  not not_1 (not_1_out, in_3);
  not not_2 (not_2_out, in_4);
  not not_3 (not_3_out, in_5);
  not not_4 (not_4_out, in_6);
  not not_5 (not_5_out, in_7);
  not not_6 (not_6_out, in_8);
  not not_7 (not_7_out, in_9);
  not not_8 (not_8_out, in_10);
  S_R_Flip_Flop s_r_ff_1 (.S(in_3), .clk(and_1_out), .R(and_2_out), .Q(s_r_ff_1_q));  // open: Qn, preset, reset, en
  and and_2 (and_2_out, not_1_out, in_11);
  S_R_Flip_Flop s_r_ff_2 (.S(in_4), .clk(and_1_out), .R(and_3_out), .Q(s_r_ff_2_q));  // open: Qn, preset, reset, en
  and and_3 (and_3_out, not_2_out, in_11);
  S_R_Flip_Flop s_r_ff_3 (.S(in_5), .clk(and_1_out), .R(and_4_out), .Q(s_r_ff_3_q));  // open: Qn, preset, reset, en
  and and_4 (and_4_out, not_3_out, in_11);
  S_R_Flip_Flop s_r_ff_4 (.S(in_6), .clk(and_1_out), .R(and_5_out), .Q(s_r_ff_4_q));  // open: Qn, preset, reset, en
  and and_5 (and_5_out, not_4_out, in_11);
  S_R_Flip_Flop s_r_ff_5 (.S(in_7), .clk(and_1_out), .R(and_6_out), .Q(s_r_ff_5_q));  // open: Qn, preset, reset, en
  and and_6 (and_6_out, not_5_out, in_11);
  S_R_Flip_Flop s_r_ff_6 (.S(in_8), .clk(and_1_out), .R(and_7_out), .Q(s_r_ff_6_q));  // open: Qn, preset, reset, en
  and and_7 (and_7_out, not_6_out, in_11);
  S_R_Flip_Flop s_r_ff_7 (.S(in_9), .clk(and_1_out), .R(and_8_out), .Q(s_r_ff_7_q));  // open: Qn, preset, reset, en
  and and_8 (and_8_out, not_7_out, in_11);
  S_R_Flip_Flop s_r_ff_8 (.S(in_10), .clk(and_1_out), .R(and_9_out), .Q(s_r_ff_8_q));  // open: Qn, preset, reset, en
  and and_9 (and_9_out, not_8_out, in_11);
  and and_10 (out_12, in_2, s_r_ff_1_q);
  and and_11 (out_13, in_2, s_r_ff_2_q);
  and and_12 (out_14, in_2, s_r_ff_3_q);
  and and_13 (out_15, in_2, s_r_ff_4_q);
  and and_14 (out_16, in_2, s_r_ff_5_q);
  and and_15 (out_17, in_2, s_r_ff_6_q);
  and and_16 (out_18, in_2, s_r_ff_7_q);
  and and_17 (out_19, in_2, s_r_ff_8_q);

  // Notes on the sheet:
  //   Byte of Memory #2
endmodule
