// Logisim project Project.circ as structural Verilog: 24 circuits, main circuit main
module main (
);

  wire _0_out, _1_out, _2_out, _3_out, _4_out, _5_out, _6_out, _7_out, _8_out, _9_out, button_1_out,
       clock_1_out, control_unit_1_address, fetch_1_gp_x, fetch_1_gp_y, not_1_out, or_1_out,
       power_supply_1_clock_out, power_supply_1_power_on, stage_counter_1_out_3, stage_counter_1_out_5,
       stage_counter_1_out_6, store_1_ram_write;
  wire [1:0] Buffer_4_out_8, fetch_1_write_2, pwr, store_1_register_write;
  wire [2:0] intruction_register_1_func_op;
  wire [3:0] alu_1_status, Buffer_2_out_8, incrementer_1_out_2, intruction_register_1_instrcacheaddr,
       intruction_register_1_opcode, multiplexer_1_out, n4_bit_register_1_read_value, pc_1_out_5,
       store_1_cache_address_2;
  wire [5:0] control_unit_1_operands;
  wire [7:0] alu_1_alu_out, alu_1_out_6, Buffer_2_out_6, Buffer_2_out_7, Buffer_3_out_6, Buffer_3_out_7,
       Buffer_3_out_8, Buffer_4_out_6, Buffer_4_out_7, Buffer_out_6, Buffer_out_7, Buffer_out_8,
       Data_Cache_out_5, fetch_1_save_register, fetch_1_val, fetch_1_x_2, fetch_1_y_2,
       gp_registers_1_read_x_value, gp_registers_1_read_y_value, Instr_Cache_out_5,
       intruction_register_1_argv_1, keypad, multiplexer_2_out, store_1_display, store_1_out_6,
       store_1_value_2;
  wire [7:2] Buffer_4_out_8_2, undriven_3;
  wire [7:3] undriven_2;
  wire [7:4] Buffer_2_out_8_2, undriven;

  Button button_1 (.out(button_1_out));
  Clock clock_1 (.out(clock_1_out));
  or or_1 (or_1_out, button_1_out, pwr[1]);
  Power_Supply power_supply_1 (
    .Toggle(pwr[0]), .Clock(clock_1_out), .Clock_Out(power_supply_1_clock_out), .Power_OFF(or_1_out),
    .Power_ON(power_supply_1_power_on));
  LED ON (.in(power_supply_1_power_on));
  Stage_Counter stage_counter_1 (
    .Clock(power_supply_1_clock_out), .out_3(stage_counter_1_out_3), .out_5(stage_counter_1_out_5),
    .out_6(stage_counter_1_out_6), .Clear(or_1_out));  // open: out_4
  PC pc_1 (
    .Update(stage_counter_1_out_6), .clock(stage_counter_1_out_6), .out_5(pc_1_out_5),
    .in_4(n4_bit_register_1_read_value), .Clear(or_1_out));
  Button _8 (.out(_8_out));
  Button _7 (.out(_7_out));
  Button _5 (.out(_5_out));
  Button _4 (.out(_4_out));
  Button _1 (.out(_1_out));
  Button _2 (.out(_2_out));
  Button _0 (.out(_0_out));
  Incrementer incrementer_1 (.in_1(pc_1_out_5), .out_2(incrementer_1_out_2));
  not not_1 (not_1_out, stage_counter_1_out_3);
  Intruction_Register intruction_register_1 (
    .in_2(pc_1_out_5), .OPCODE(intruction_register_1_opcode), .argv_1(intruction_register_1_argv_1),
    .instrcacheaddr(intruction_register_1_instrcacheaddr), .instrval(Instr_Cache_out_5),
    .func_OP(intruction_register_1_func_op), .NOP_Stage(not_1_out));
  Cache Instr_Cache (
    .in_4(power_supply_1_clock_out), .out_5(Instr_Cache_out_5), .status(1'b0),
    .raddress(intruction_register_1_instrcacheaddr));  // open: writeval
  Button _9 (.out(_9_out));
  Button _6 (.out(_6_out));
  Button _3 (.out(_3_out));
  Control_Unit control_unit_1 (
    .OPERANDS(control_unit_1_operands), .address(control_unit_1_address), .OPCODE(Buffer_out_6[3:0]),
    .\function (Buffer_out_7[2:0]), .Stop(pwr));
  Buffer Buffer (
    .in_3({undriven, intruction_register_1_opcode}), .in_4({undriven_2, intruction_register_1_func_op}),
    .in_5(intruction_register_1_argv_1), .out_6(Buffer_out_6), .out_7(Buffer_out_7), .out_8(Buffer_out_8),
    .in_1(power_supply_1_clock_out), .Clear(or_1_out));
  Keypad u_KeyPad (
    ._7(_7_out), ._8(_8_out), ._9(_9_out), ._4(_4_out), ._5(_5_out), ._6(_6_out), ._1(_1_out), ._2(_2_out),
    ._3(_3_out), ._0(_0_out), .out_11(keypad));
  GP_Registers gp_registers_1 (
    .Y_Address(fetch_1_gp_y), .Read_X_Value(gp_registers_1_read_x_value),
    .Read_Y_Value(gp_registers_1_read_y_value), .writeval(fetch_1_val), .write(fetch_1_write_2),
    .clock(power_supply_1_clock_out), .X_Address(fetch_1_gp_x));
  Fetch fetch_1 (
    .X_2(fetch_1_x_2), .Y_2(fetch_1_y_2), .X(gp_registers_1_read_x_value), .Y(gp_registers_1_read_y_value),
    .GP_x(fetch_1_gp_x), .GP_y(fetch_1_gp_y), .writeval(Buffer_4_out_7), .val(fetch_1_val),
    .address(control_unit_1_address), .address_2(Buffer_out_8), .save_register(fetch_1_save_register[0]),
    .write(Buffer_4_out_8), .write_2(fetch_1_write_2));
  Buffer Buffer_2 (
    .in_3({fetch_1_save_register[7], control_unit_1_operands, fetch_1_save_register[0]}), .in_4(fetch_1_x_2),
    .in_5(fetch_1_y_2), .out_6(Buffer_2_out_6), .out_7(Buffer_2_out_7),
    .out_8({Buffer_2_out_8_2, Buffer_2_out_8}), .in_1(power_supply_1_clock_out), .Clear(or_1_out));
  ALU alu_1 (
    .out_6(alu_1_out_6), .in_1(Buffer_2_out_6), .ALU_OUT(alu_1_alu_out), .in_2(Buffer_2_out_7),
    .in_3({Buffer_2_out_8_2, Buffer_2_out_8}), .Status(alu_1_status), .clock(power_supply_1_clock_out),
    .clear(or_1_out));
  Multiplexer #(.width(4)) multiplexer_1 (
    .in0(incrementer_1_out_2), .in1(Buffer_2_out_8), .out(multiplexer_1_out), .sel(alu_1_status[2]));  // open: en
  _4_Bit_Register u_4_bit_register_1 (
    .Write_Value(multiplexer_1_out), .Read_Value(n4_bit_register_1_read_value),
    .write(stage_counter_1_out_5), .clock(power_supply_1_clock_out));  // open: Clear
  Multiplexer #(.width(8)) multiplexer_2 (
    .in0(alu_1_alu_out), .in1(keypad), .out(multiplexer_2_out), .sel(alu_1_out_6[6]));  // open: en
  Buffer Buffer_3 (
    .in_3(alu_1_out_6), .in_4(multiplexer_2_out), .in_5({Buffer_2_out_8_2, Buffer_2_out_8}),
    .out_6(Buffer_3_out_6), .out_7(Buffer_3_out_7), .out_8(Buffer_3_out_8), .in_1(power_supply_1_clock_out),
    .Clear(or_1_out));
  Store store_1 (
    .OPERANDS(Buffer_3_out_6), .value(Buffer_3_out_7), .cache_address(Buffer_3_out_8),
    .Display(store_1_display[0]), .out_6(store_1_out_6), .value_2(store_1_value_2),
    .cache_address_2(store_1_cache_address_2), .ram_write(store_1_ram_write),
    .register_write(store_1_register_write), .cache_val(Data_Cache_out_5));
  Cache Data_Cache (
    .in_4(power_supply_1_clock_out), .out_5(Data_Cache_out_5), .status(store_1_ram_write),
    .writeval(store_1_value_2), .raddress(store_1_cache_address_2));
  Buffer Buffer_4 (
    .in_3(store_1_display), .in_4(store_1_out_6), .in_5({undriven_3, store_1_register_write}),
    .out_6(Buffer_4_out_6), .out_7(Buffer_4_out_7), .out_8({Buffer_4_out_8_2, Buffer_4_out_8}),
    .in_1(power_supply_1_clock_out), .Clear(or_1_out));
  Digit_Display digit_display_1 (.Value(Buffer_4_out_7), .Update(Buffer_4_out_6[0]), .Clock(power_supply_1_clock_out));

  // Notes on the sheet:
  //   EGO
  //   PC Buffer
  //   Developped by:
  //   Charley-Roy, Dominic - 260526659
  //   Denis, Xavier - 260521681
  //   Weiss, Martin - 260405962
endmodule

module Intruction_Register (
  input  NOP_Stage,
  input  [3:0] in_2,
  input  [7:0] instrval,
  output [3:0] OPCODE,
  output [2:0] func_OP,
  output [7:0] argv_1,
  output [3:0] instrcacheaddr
);

  Multiplexer #(.width(8)) multiplexer_1 (
    .in0(instrval), .in1({8{1'b0}}), .out({OPCODE[2:0], argv_1[0], argv_1[7:4]}), .sel(NOP_Stage));  // open: en

  assign func_OP = argv_1[6:4];
  assign instrcacheaddr = in_2;
endmodule

module Half_Adder (
  input  in_1,
  input  in_2,
  output out_3,
  output out_4
);

  wire not_1_out, or_1_out;

  or or_1 (or_1_out, in_1, in_2);
  and and_1 (out_4, in_1, in_2);
  and and_2 (out_3, or_1_out, not_1_out);
  not not_1 (not_1_out, out_4);
endmodule

module Full_Adder (
  input  in_1,
  input  in_2,
  input  in_3,
  output out_4,
  output out_5
);

  wire half_adder_1_out_3, half_adder_1_out_4, half_adder_2_out_4;

  Half_Adder half_adder_1 (.in_1(in_1), .in_2(in_2), .out_3(half_adder_1_out_3), .out_4(half_adder_1_out_4));
  Half_Adder half_adder_2 (.in_1(half_adder_1_out_3), .in_2(in_3), .out_3(out_4), .out_4(half_adder_2_out_4));
  or or_1 (out_5, half_adder_2_out_4, half_adder_1_out_4);
endmodule

module Addition (
  input  [7:0] Left,
  input  [7:0] Right,
  output [7:0] Add_Result,
  output [1:0] Status
);

  wire full_adder_1_out_5, full_adder_2_out_5, full_adder_3_out_5, full_adder_4_out_5, full_adder_5_out_5,
       full_adder_6_out_5, half_adder_1_out_4, or_1_out;

  Half_Adder half_adder_1 (.in_1(Left[0]), .in_2(Right[0]), .out_3(Add_Result[0]), .out_4(half_adder_1_out_4));
  Full_Adder full_adder_1 (
    .in_1(half_adder_1_out_4), .in_2(Right[1]), .in_3(Left[1]), .out_4(Add_Result[1]),
    .out_5(full_adder_1_out_5));
  Full_Adder full_adder_2 (
    .in_1(full_adder_1_out_5), .in_2(Right[2]), .in_3(Left[2]), .out_4(Add_Result[2]),
    .out_5(full_adder_2_out_5));
  Full_Adder full_adder_3 (
    .in_1(full_adder_2_out_5), .in_2(Right[3]), .in_3(Left[3]), .out_4(Add_Result[3]),
    .out_5(full_adder_3_out_5));
  Full_Adder full_adder_4 (
    .in_1(full_adder_3_out_5), .in_2(Right[4]), .in_3(Left[4]), .out_4(Add_Result[4]),
    .out_5(full_adder_4_out_5));
  Full_Adder full_adder_5 (
    .in_1(full_adder_4_out_5), .in_2(Right[5]), .in_3(Left[5]), .out_4(Add_Result[5]),
    .out_5(full_adder_5_out_5));
  Full_Adder full_adder_6 (
    .in_1(full_adder_5_out_5), .in_2(Right[6]), .in_3(Left[6]), .out_4(Add_Result[6]),
    .out_5(full_adder_6_out_5));
  Full_Adder full_adder_7 (
    .in_1(full_adder_6_out_5), .in_2(Right[7]), .in_3(Left[7]), .out_4(Add_Result[7]), .out_5(Status[0]));
  or or_1 (or_1_out, Add_Result[7], Add_Result[6], Add_Result[5], Add_Result[4], Add_Result[3], Add_Result[2], Add_Result[1], Add_Result[0]);
  not not_1 (Status[1], or_1_out);

  // Notes on the sheet:
  //   Overflow
  //   Zero?
  //   ALU-Out
endmodule

module _2_s_Complement (
  input  [7:0] in_1,
  output [7:0] out_2
);

  wire half_adder_1_out_4, half_adder_2_out_4, half_adder_3_out_4, half_adder_4_out_4, half_adder_5_out_4,
       half_adder_6_out_4, half_adder_7_out_4, not_1_out, not_2_out, not_3_out, not_4_out, not_5_out,
       not_6_out, not_7_out, not_8_out, not_9_out, or_1_out;

  not not_1 (not_1_out, in_1[6]);
  not not_2 (not_2_out, in_1[7]);
  not not_3 (not_3_out, in_1[2]);
  not not_4 (not_4_out, in_1[4]);
  not not_5 (not_5_out, in_1[5]);
  not not_6 (not_6_out, in_1[3]);
  not not_7 (not_7_out, not_9_out);
  not not_8 (not_8_out, in_1[1]);
  not not_9 (not_9_out, in_1[0]);
  or or_1 (or_1_out, not_7_out, not_9_out);
  Half_Adder half_adder_1 (.in_1(or_1_out), .in_2(not_9_out), .out_3(out_2[0]), .out_4(half_adder_1_out_4));
  Half_Adder half_adder_2 (.in_1(half_adder_1_out_4), .in_2(not_8_out), .out_3(out_2[1]), .out_4(half_adder_2_out_4));
  Half_Adder half_adder_3 (.in_1(half_adder_2_out_4), .in_2(not_3_out), .out_3(out_2[2]), .out_4(half_adder_3_out_4));
  Half_Adder half_adder_4 (.in_1(half_adder_3_out_4), .in_2(not_6_out), .out_3(out_2[3]), .out_4(half_adder_4_out_4));
  Half_Adder half_adder_5 (.in_1(half_adder_4_out_4), .in_2(not_4_out), .out_3(out_2[4]), .out_4(half_adder_5_out_4));
  Half_Adder half_adder_6 (.in_1(half_adder_5_out_4), .in_2(not_5_out), .out_3(out_2[5]), .out_4(half_adder_6_out_4));
  Half_Adder half_adder_7 (.in_1(half_adder_6_out_4), .in_2(not_1_out), .out_3(out_2[6]), .out_4(half_adder_7_out_4));
  Half_Adder half_adder_8 (.in_1(half_adder_7_out_4), .in_2(not_2_out), .out_3(out_2[7]));  // open: out_4
endmodule

module ALU (
  input  [7:0] in_1,
  input  [7:0] in_2,
  input  [7:0] in_3,
  input  clock,
  input  clear,
  output [7:0] out_6,
  output [7:0] ALU_OUT,
  output [3:0] Status
);

  wire and_2_out, and_3_out, and_4_out, and_5_out, and_6_out, and_7_out, zero_1_out_2;
  wire [1:0] or_1_out;
  wire [1:1] addition_1_status;
  wire [7:0] addition_1_add_result, multiplexer_1_out, multiplexer_2_out, multiplication_1_hi,
       multiplication_1_lo, n2_s_complement_1_out_2, n8_bit_register_1_out_5;

  _2_s_Complement u_2_s_complement_1 (.in_1(in_3), .out_2(n2_s_complement_1_out_2));
  Multiplexer #(.width(8)) multiplexer_1 (
    .in0(in_3), .in1(n2_s_complement_1_out_2), .out(multiplexer_1_out), .sel(and_3_out));  // open: en
  // AND_Gate and_1 has open pins: in0=in_1[3], in1=in_1[2], in2=in_1[1], out=open
  Addition addition_1 (
    .Add_Result(addition_1_add_result), .Left(multiplexer_1_out), .Right(in_2),
    .Status({addition_1_status[1], Status[0]}));
  Multiplication multiplication_1 (.A(in_2), .B(in_3), .HI(multiplication_1_hi), .LO(multiplication_1_lo));
  and and_2 (and_2_out, ~in_1[3], ~in_1[2], in_1[1]);  // AND_Gate
  and and_3 (and_3_out, ~in_1[3], in_1[2], ~in_1[1]);  // AND_Gate
  and and_4 (and_4_out, ~in_1[3], in_1[2], in_1[1]);  // AND_Gate
  or or_1 (or_1_out[0], and_2_out, and_3_out, and_5_out);
  _8_Bit_Register u_8_bit_register_1 (
    .in_4(multiplication_1_hi), .out_5(n8_bit_register_1_out_5), .Clear(clear), .write(and_5_out),
    .clock(clock));
  and and_5 (and_5_out, in_1[3], ~in_1[2], ~in_1[1]);  // AND_Gate
  and and_6 (and_6_out, in_1[3], ~in_1[2], in_1[1]);  // AND_Gate
  or or_2 (or_1_out[1], and_4_out, and_5_out);
  Multiplexer #(.select(2), .width(8)) multiplexer_2 (
    .in0(in_2), .in1(addition_1_add_result), .in2(n2_s_complement_1_out_2), .in3(multiplication_1_lo),
    .out(multiplexer_2_out), .sel(or_1_out));  // open: en
  Multiplexer #(.width(8)) multiplexer_3 (
    .in0(multiplexer_2_out), .in1(n8_bit_register_1_out_5), .out(ALU_OUT), .sel(and_6_out));  // open: en
  and and_7 (and_7_out, in_1[3], in_1[2], ~in_1[1]);  // AND_Gate
  // AND_Gate and_8 has open pins: in0=in_1[3], in1=in_1[2], in2=in_1[1], out=open
  Zero zero_1 (.in_1(ALU_OUT), .out_2(zero_1_out_2));
  or or_3 (Status[1], addition_1_status[1], zero_1_out_2);
  and and_9 (Status[2], and_7_out, Status[1]);

  assign out_6 = in_1;

  // Notes on the sheet:
  //   NOP
  //   ADD
  //   SUB
  //   MULT
  //   MULT-OVERFLOW
  //   OPERATIONS
  //   000
  //   001
  //   010
  //   011
  //   COMP ( -)
  //   100
  //   101
  //   110
  //   BRE0
  //   default state
  //   Bit 0 - Overflow
  //   Bit 1 - Zero
  //   Bit 2 - Branch?
endmodule

module GP_Registers (
  input  X_Address,
  input  Y_Address,
  input  [7:0] writeval,
  input  [1:0] write,
  input  clock,
  output [7:0] Read_X_Value,
  output [7:0] Read_Y_Value
);

  wire decoder_1_out0, decoder_1_out1;
  wire [7:0] demultiplexer_1_out0, demultiplexer_1_out1, n8_bit_register_1_out_5, n8_bit_register_2_out_5;

  Demultiplexer #(.width(8)) demultiplexer_1 (
    .out0(demultiplexer_1_out0), .out1(demultiplexer_1_out1), .in(writeval), .sel(write[1]), .en(write[0]));
  Decoder decoder_1 (.out0(decoder_1_out0), .out1(decoder_1_out1), .sel(write[1]), .en(write[0]));
  _8_Bit_Register u_8_bit_register_1 (
    .in_4(demultiplexer_1_out0), .out_5(n8_bit_register_1_out_5), .write(decoder_1_out0), .clock(clock));  // open: Clear
  _8_Bit_Register u_8_bit_register_2 (
    .in_4(demultiplexer_1_out1), .out_5(n8_bit_register_2_out_5), .write(decoder_1_out1), .clock(clock));  // open: Clear
  Multiplexer #(.width(8)) multiplexer_1 (
    .in0(n8_bit_register_1_out_5), .in1(n8_bit_register_2_out_5), .out(Read_X_Value), .sel(X_Address));  // open: en
  Multiplexer #(.width(8)) multiplexer_2 (
    .in0(n8_bit_register_1_out_5), .in1(n8_bit_register_2_out_5), .out(Read_Y_Value), .sel(Y_Address));  // open: en

  // Notes on the sheet:
  //   First bit says what register to write to
  //   Second write bit says whether we are writing
endmodule

module _8_Bit_Register (
  input  Clear,
  input  write,
  input  clock,
  input  [7:0] in_4,
  output [7:0] out_5
);

  wire and_1_out, not_1_out, not_2_out, not_3_out, not_4_out, not_5_out, not_6_out, not_7_out, not_8_out;

  and and_1 (and_1_out, write, clock);
  not not_1 (not_1_out, in_4[0]);
  not not_2 (not_2_out, in_4[1]);
  not not_3 (not_3_out, in_4[2]);
  not not_4 (not_4_out, in_4[3]);
  not not_5 (not_5_out, in_4[4]);
  not not_6 (not_6_out, in_4[5]);
  not not_7 (not_7_out, in_4[6]);
  not not_8 (not_8_out, in_4[7]);
  S_R_Flip_Flop s_r_ff_1 (
    .S(in_4[0]), .clk(and_1_out), .R(not_1_out), .Q(out_5[0]), .reset(Clear));  // open: Qn, preset, en
  S_R_Flip_Flop s_r_ff_2 (
    .S(in_4[1]), .clk(and_1_out), .R(not_2_out), .Q(out_5[1]), .reset(Clear));  // open: Qn, preset, en
  S_R_Flip_Flop s_r_ff_3 (
    .S(in_4[2]), .clk(and_1_out), .R(not_3_out), .Q(out_5[2]), .reset(Clear));  // open: Qn, preset, en
  S_R_Flip_Flop s_r_ff_4 (
    .S(in_4[3]), .clk(and_1_out), .R(not_4_out), .Q(out_5[3]), .reset(Clear));  // open: Qn, preset, en
  S_R_Flip_Flop s_r_ff_5 (
    .S(in_4[4]), .clk(and_1_out), .R(not_5_out), .Q(out_5[4]), .reset(Clear));  // open: Qn, preset, en
  S_R_Flip_Flop s_r_ff_6 (
    .S(in_4[5]), .clk(and_1_out), .R(not_6_out), .Q(out_5[5]), .reset(Clear));  // open: Qn, preset, en
  S_R_Flip_Flop s_r_ff_7 (
    .S(in_4[6]), .clk(and_1_out), .R(not_7_out), .Q(out_5[6]), .reset(Clear));  // open: Qn, preset, en
  S_R_Flip_Flop s_r_ff_8 (
    .S(in_4[7]), .clk(and_1_out), .R(not_8_out), .Q(out_5[7]), .reset(Clear));  // open: Qn, preset, en
endmodule

module Control_Unit (
  input  [3:0] OPCODE,
  input  [2:0] \function ,
  output [1:0] Stop,
  output address,
  output [5:0] OPERANDS
);

  wire and_2_out, and_3_out, and_4_out, and_5_out, and_6_out, and_7_out, and_8_out, not_1_out, or_2_out;
  wire [2:0] multiplexer_1_out;

  // AND_Gate and_1 has open pins: in0=OPCODE[2], in1=OPCODE[1], in2=OPCODE[0], out=open
  and and_2 (and_2_out, ~OPCODE[2], OPCODE[1], ~OPCODE[0]);  // AND_Gate
  and and_3 (and_3_out, ~OPCODE[2], ~OPCODE[1], OPCODE[0]);  // AND_Gate
  and and_4 (and_4_out, ~OPCODE[2], OPCODE[1], OPCODE[0]);  // AND_Gate
  and and_5 (and_5_out, OPCODE[2], ~OPCODE[1], ~OPCODE[0]);  // AND_Gate
  and and_6 (and_6_out, OPCODE[2], OPCODE[1], ~OPCODE[0]);  // AND_Gate
  and and_7 (and_7_out, OPCODE[2], ~OPCODE[1], OPCODE[0]);  // AND_Gate
  Multiplexer #(.width(3)) multiplexer_1 (
    .in0(3'b000), .in1(3'b110), .out(multiplexer_1_out), .sel(and_7_out));  // open: en
  and and_8 (and_8_out, OPCODE[2], OPCODE[1], OPCODE[0]);
  or or_1 (address, and_2_out, and_7_out, and_3_out);
  Multiplexer #(.width(3)) multiplexer_2 (
    .in0(multiplexer_1_out), .in1(\function ), .out(OPERANDS[2:0]), .sel(and_8_out));  // open: en
  or or_2 (or_2_out, \function [0], \function [1], \function [2]);
  or or_3 (OPERANDS[3], and_8_out, and_2_out, and_5_out);
  or or_4 (OPERANDS[4], and_5_out, and_3_out);
  or or_5 (OPERANDS[5], and_4_out, and_2_out);
  and and_9 (Stop[0], and_6_out, not_1_out);
  not not_1 (not_1_out, or_2_out);
  and and_10 (Stop[1], and_6_out, or_2_out);

  // Notes on the sheet:
  //   OPERANDS
  //   Bit 0 - ALU
  //   Bit 1 - ALU
  //   Bit 2 - Address?
  //   Bit 3 - write?
  //   NOP
  //   000
  //   LOAD
  //   STORE
  //   010
  //   001
  //   PRINT
  //   READ
  //   100
  //   011
  //   BRANCH
  //   STOP
  //   110
  //   101
  //   ALU
  //   111
  //   Bit 0 = STOP opcode
  //   Bit 1 = HALT opcode - When any function other than zero
endmodule

module Cache (
  input  [7:0] writeval,
  input  status,
  input  [3:0] raddress,
  input  in_4,
  output [7:0] out_5
);

  wire and_1_out, and_2_out, and_3_out, and_4_out, and_5_out, and_6_out, and_7_out, and_8_out, and_9_out,
       and_10_out, and_11_out, and_12_out, and_13_out, and_14_out, and_15_out, and_16_out,
       demultiplexer_1_out0, demultiplexer_1_out1, demultiplexer_1_out2, demultiplexer_1_out3, not_1_out,
       not_2_out, not_3_out, not_4_out, not_5_out, not_6_out, not_7_out, not_8_out, not_9_out, not_10_out,
       not_11_out, not_12_out, not_13_out, not_14_out, not_15_out, not_16_out;
  wire [7:0] _00_read_val, cache_byte_3_read_val, cache_byte_7_read_val, cache_byte_11_read_val;

  Demultiplexer #(.select(2)) demultiplexer_1 (
    .out0(demultiplexer_1_out0), .out1(demultiplexer_1_out1), .out2(demultiplexer_1_out2),
    .out3(demultiplexer_1_out3), .in(status), .sel(raddress[3:2]));  // open: en
  not not_1 (not_1_out, raddress[0]);
  not not_2 (not_2_out, raddress[1]);
  not not_3 (not_3_out, raddress[1]);
  not not_4 (not_4_out, raddress[0]);
  Cache_Byte _00 (
    .status(demultiplexer_1_out0), .address(and_1_out), .write_val(writeval), .read_val(_00_read_val),
    .in_4(in_4));
  and and_1 (and_1_out, not_1_out, not_2_out);
  Cache_Byte _01 (
    .status(demultiplexer_1_out0), .address(and_2_out), .write_val(writeval), .read_val(_00_read_val),
    .in_4(in_4));
  and and_2 (and_2_out, raddress[0], not_3_out);
  Cache_Byte cache_byte_1 (
    .status(demultiplexer_1_out0), .address(and_3_out), .write_val(writeval), .read_val(_00_read_val),
    .in_4(in_4));
  and and_3 (and_3_out, not_4_out, raddress[1]);
  Cache_Byte cache_byte_2 (
    .status(demultiplexer_1_out0), .address(and_4_out), .write_val(writeval), .read_val(_00_read_val),
    .in_4(in_4));
  and and_4 (and_4_out, raddress[0], raddress[1]);
  not not_5 (not_5_out, raddress[0]);
  not not_6 (not_6_out, raddress[1]);
  not not_7 (not_7_out, raddress[1]);
  not not_8 (not_8_out, raddress[0]);
  and and_5 (and_5_out, not_5_out, not_6_out);
  Cache_Byte cache_byte_3 (
    .status(demultiplexer_1_out1), .address(and_5_out), .write_val(writeval),
    .read_val(cache_byte_3_read_val), .in_4(in_4));
  and and_6 (and_6_out, raddress[0], not_7_out);
  Cache_Byte cache_byte_4 (
    .status(demultiplexer_1_out1), .address(and_6_out), .write_val(writeval),
    .read_val(cache_byte_3_read_val), .in_4(in_4));
  Cache_Byte cache_byte_5 (
    .status(demultiplexer_1_out1), .address(and_7_out), .write_val(writeval),
    .read_val(cache_byte_3_read_val), .in_4(in_4));
  and and_7 (and_7_out, not_8_out, raddress[1]);
  Cache_Byte cache_byte_6 (
    .status(demultiplexer_1_out1), .address(and_8_out), .write_val(writeval),
    .read_val(cache_byte_3_read_val), .in_4(in_4));
  and and_8 (and_8_out, raddress[0], raddress[1]);
  not not_9 (not_9_out, raddress[0]);
  and and_9 (and_9_out, not_9_out, not_10_out);
  not not_10 (not_10_out, raddress[1]);
  and and_10 (and_10_out, raddress[0], not_11_out);
  not not_11 (not_11_out, raddress[1]);
  not not_12 (not_12_out, raddress[0]);
  and and_11 (and_11_out, not_12_out, raddress[1]);
  and and_12 (and_12_out, raddress[0], raddress[1]);
  Multiplexer #(.select(2), .width(8)) multiplexer_1 (
    .in0(_00_read_val), .in1(cache_byte_3_read_val), .in2(cache_byte_7_read_val),
    .in3(cache_byte_11_read_val), .out(out_5), .sel(raddress[3:2]));  // open: en
  Cache_Byte cache_byte_7 (
    .status(demultiplexer_1_out2), .address(and_9_out), .write_val(writeval),
    .read_val(cache_byte_7_read_val), .in_4(in_4));
  Cache_Byte cache_byte_8 (
    .status(demultiplexer_1_out2), .address(and_10_out), .write_val(writeval),
    .read_val(cache_byte_7_read_val), .in_4(in_4));
  Cache_Byte cache_byte_9 (
    .status(demultiplexer_1_out2), .address(and_11_out), .write_val(writeval),
    .read_val(cache_byte_7_read_val), .in_4(in_4));
  Cache_Byte cache_byte_10 (
    .status(demultiplexer_1_out2), .address(and_12_out), .write_val(writeval),
    .read_val(cache_byte_7_read_val), .in_4(in_4));
  not not_13 (not_13_out, raddress[0]);
  and and_13 (and_13_out, not_13_out, not_14_out);
  not not_14 (not_14_out, raddress[1]);
  and and_14 (and_14_out, raddress[0], not_15_out);
  not not_15 (not_15_out, raddress[1]);
  not not_16 (not_16_out, raddress[0]);
  and and_15 (and_15_out, not_16_out, raddress[1]);
  and and_16 (and_16_out, raddress[0], raddress[1]);
  Cache_Byte cache_byte_11 (
    .status(demultiplexer_1_out3), .address(and_13_out), .write_val(writeval),
    .read_val(cache_byte_11_read_val), .in_4(in_4));
  Cache_Byte cache_byte_12 (
    .status(demultiplexer_1_out3), .address(and_14_out), .write_val(writeval),
    .read_val(cache_byte_11_read_val), .in_4(in_4));
  Cache_Byte cache_byte_13 (
    .status(demultiplexer_1_out3), .address(and_15_out), .write_val(writeval),
    .read_val(cache_byte_11_read_val), .in_4(in_4));
  Cache_Byte cache_byte_14 (
    .status(demultiplexer_1_out3), .address(and_16_out), .write_val(writeval),
    .read_val(cache_byte_11_read_val), .in_4(in_4));
endmodule

module Cache_Byte (
  input  status,
  input  address,
  input  [7:0] write_val,
  input  in_4,
  output [7:0] read_val
);

  wire and_1_out, and_2_out, not_1_out, not_2_out, not_3_out, not_4_out, not_5_out, not_6_out, not_7_out,
       not_8_out;
  wire [7:0] s_r_ff_1_q;

  and and_1 (and_1_out, status, address);
  not not_1 (not_1_out, write_val[0]);
  not not_2 (not_2_out, write_val[1]);
  not not_3 (not_3_out, write_val[2]);
  not not_4 (not_4_out, write_val[3]);
  not not_5 (not_5_out, write_val[4]);
  not not_6 (not_6_out, write_val[5]);
  not not_7 (not_7_out, write_val[6]);
  not not_8 (not_8_out, write_val[7]);
  and and_2 (and_2_out, and_1_out, in_4);
  S_R_Flip_Flop s_r_ff_1 (
    .S(write_val[0]), .clk(and_2_out), .R(not_1_out), .Q(s_r_ff_1_q[0]));  // open: Qn, preset, reset, en
  S_R_Flip_Flop s_r_ff_2 (
    .S(write_val[1]), .clk(and_2_out), .R(not_2_out), .Q(s_r_ff_1_q[1]));  // open: Qn, preset, reset, en
  S_R_Flip_Flop s_r_ff_3 (
    .S(write_val[2]), .clk(and_2_out), .R(not_3_out), .Q(s_r_ff_1_q[2]));  // open: Qn, preset, reset, en
  S_R_Flip_Flop s_r_ff_4 (
    .S(write_val[3]), .clk(and_2_out), .R(not_4_out), .Q(s_r_ff_1_q[3]));  // open: Qn, preset, reset, en
  S_R_Flip_Flop s_r_ff_5 (
    .S(write_val[4]), .clk(and_2_out), .R(not_5_out), .Q(s_r_ff_1_q[4]));  // open: Qn, preset, reset, en
  S_R_Flip_Flop s_r_ff_6 (
    .S(write_val[5]), .clk(and_2_out), .R(not_6_out), .Q(s_r_ff_1_q[5]));  // open: Qn, preset, reset, en
  S_R_Flip_Flop s_r_ff_7 (
    .S(write_val[6]), .clk(and_2_out), .R(not_7_out), .Q(s_r_ff_1_q[6]));  // open: Qn, preset, reset, en
  S_R_Flip_Flop s_r_ff_8 (
    .S(write_val[7]), .clk(and_2_out), .R(not_8_out), .Q(s_r_ff_1_q[7]));  // open: Qn, preset, reset, en
  assign read_val = address ? s_r_ff_1_q : 8'bz;  // Controlled_Buffer controlled_buffer_1

  // Notes on the sheet:
  //   Least Significant Bit
  //   Bit 0
  //   Bit 1
  //   Bit 2
  //   Bit 3
  //   Bit 4
  //   Bit 5
  //   Bit 6
  //   Bit 7
  //   INSTRUCTIONS DEFINED IN ASSEMBLY*
  //   To write an instruction:
  //   EXAMPLE INSTRUCTION:
  //   EXAMPLE ALU INSTRUCTION:
  //   ALU-Operation ADD R0 = R0 + R1
  //   *Note: Applicable in Instruction Cache only
  //   Least Significant Bit
  //   Begin writing from most significant (bottom) to least significant (up).
  //   Format: 110 0 1 001 [opcode][alu-L][alu-R][funct]
  //   MULT-OVERFLOW 101
  //   Each instruction is 8 bits. Notation [2-0] represents 3 least-significant bits (so bit 2, 1 and 0)
  //   STORE (001) from register 0, into the byte addressed by 1100 in data cache.
  //   Format: 00101100 == [001][0][1100] == [opcode][register to read][address in data cache]
  //   OPCODES:
  //   STOP: [110]
  //   STORE: [001]
  //   LOAD: [010]
  //   PRINT: [100]
  //   READ: [011]
  //   NOP:[000]
  //   BRANCH: [101]
  //   ALU: [111]
  //   ALU FUNCTIONAL OPCODES:
  //   NOP: 000
  //   ADD: 001
  //   SUB: 010
  //   COMP: 011
  //   MULT: 100
  //   BREQ: 110
endmodule

module Fetch (
  input  address,
  input  [7:0] address_2,
  input  [7:0] X,
  input  [7:0] Y,
  input  [7:0] writeval,
  input  [1:0] write,
  output save_register,
  output [7:0] X_2,
  output [7:0] Y_2,
  output [7:0] val,
  output GP_x,
  output GP_y,
  output [1:0] write_2
);

  wire not_1_out;
  wire [7:0] bit_extender_1_out;

  assign bit_extender_1_out = {{4{1'b0}}, address_2[7:4]};  // Bit_Extender bit_extender_1
  not not_1 (not_1_out, address);
  Multiplexer #(.width(8)) multiplexer_1 (.in0(bit_extender_1_out), .in1(Y), .out(Y_2), .sel(not_1_out));  // open: en

  assign GP_x = address_2[0];
  assign GP_y = address_2[7];
  assign save_register = address_2[0];
  assign val = writeval;
  assign write_2 = write;
  assign X_2 = X;
endmodule

module Store (
  input  [7:0] OPERANDS,
  input  [7:0] value,
  input  [7:0] cache_address,
  input  [7:0] cache_val,
  output Display,
  output [7:0] out_6,
  output [7:0] value_2,
  output [3:0] cache_address_2,
  output ram_write,
  output [1:0] register_write
);

  wire and_2_out, and_3_out;

  and and_1 (ram_write, OPERANDS[5], ~OPERANDS[4]);  // AND_Gate
  and and_2 (and_2_out, ~OPERANDS[5], OPERANDS[4]);  // AND_Gate
  or or_1 (register_write[0], and_2_out, OPERANDS[6]);
  and and_3 (and_3_out, OPERANDS[6], OPERANDS[4]);
  Multiplexer #(.width(8)) multiplexer_1 (.in0(value), .in1(cache_val), .out(out_6), .sel(and_3_out));  // open: en
  and and_4 (Display, OPERANDS[4], OPERANDS[5]);

  assign cache_address_2 = cache_address[3:0];
  assign register_write[1] = OPERANDS[0];
  assign value_2 = value;
endmodule

module Buffer (
  input  in_1,
  input  Clear,
  input  [7:0] in_3,
  input  [7:0] in_4,
  input  [7:0] in_5,
  output [7:0] out_6,
  output [7:0] out_7,
  output [7:0] out_8
);

  _8_Bit_Register u_8_bit_register_1 (.in_4(in_5), .out_5(out_8), .Clear(Clear), .write(in_1), .clock(in_1));
  _8_Bit_Register u_8_bit_register_2 (.in_4(in_3), .out_5(out_6), .Clear(Clear), .write(in_1), .clock(in_1));
  _8_Bit_Register u_8_bit_register_3 (.in_4(in_4), .out_5(out_7), .Clear(Clear), .write(in_1), .clock(in_1));
endmodule

module aluswitcher (
  input  in_1,
  input  [7:0] in_2,
  input  [7:0] in_3,
  output [7:0] out_4,
  output [7:0] out_5
);

  wire not_1_out;
  wire [7:0] demultiplexer_1_out0;

  not not_1 (not_1_out, in_1);
  Demultiplexer #(.width(8)) demultiplexer_1 (
    .out0(demultiplexer_1_out0), .out1(out_5), .in(in_3), .sel(in_1));  // open: en
  Multiplexer #(.width(8), .enable("false")) multiplexer_1 (
    .in0(in_2), .in1(demultiplexer_1_out0), .out(out_4), .sel(not_1_out));
endmodule

module Digit_Display (
  input  Update,
  input  Clock,
  input  [7:0] Value
);

  wire and_1_out, and_2_out, and_3_out, and_4_out, and_5_out, and_6_out, and_7_out, and_8_out, and_9_out,
       and_10_out, and_11_out, and_12_out, and_13_out, and_14_out, and_15_out, not_1_out, not_2_out,
       not_3_out, not_4_out, not_5_out, not_6_out, not_7_out, not_8_out, not_9_out, not_10_out, not_11_out,
       not_12_out, not_13_out, not_14_out, not_15_out, not_16_out, not_17_out, not_18_out, not_19_out,
       not_20_out, not_21_out, not_22_out, not_23_out, not_24_out, not_25_out, not_26_out, not_27_out,
       not_28_out, not_29_out, not_30_out, not_31_out, not_32_out, not_33_out, not_34_out, not_35_out,
       not_36_out, not_37_out, not_38_out, not_39_out, not_40_out, not_41_out, not_42_out, not_43_out,
       or_1_out, or_2_out, or_3_out, or_4_out, or_5_out, or_6_out;
  wire [7:0] multiplexer_1_out, n2_s_complement_1_out_2, n8_bit_register_1_out_5;

  _8_Bit_Register u_8_bit_register_1 (
    .in_4(Value), .out_5(n8_bit_register_1_out_5), .write(Update), .clock(Clock));  // open: Clear
  _2_s_Complement u_2_s_complement_1 (.in_1(n8_bit_register_1_out_5), .out_2(n2_s_complement_1_out_2));
  Multiplexer #(.width(8)) multiplexer_1 (
    .in0(n8_bit_register_1_out_5), .in1(n2_s_complement_1_out_2), .out(multiplexer_1_out),
    .sel(n8_bit_register_1_out_5[7]));  // open: en
  not not_1 (not_1_out, multiplexer_1_out[0]);
  not not_2 (not_2_out, multiplexer_1_out[1]);
  not not_3 (not_3_out, multiplexer_1_out[3]);
  not not_4 (not_4_out, multiplexer_1_out[1]);
  not not_5 (not_5_out, multiplexer_1_out[2]);
  not not_6 (not_6_out, multiplexer_1_out[3]);
  not not_7 (not_7_out, multiplexer_1_out[0]);
  not not_8 (not_8_out, multiplexer_1_out[3]);
  not not_9 (not_9_out, multiplexer_1_out[1]);
  not not_10 (not_10_out, multiplexer_1_out[3]);
  not not_11 (not_11_out, multiplexer_1_out[0]);
  not not_12 (not_12_out, multiplexer_1_out[2]);
  not not_13 (not_13_out, multiplexer_1_out[3]);
  not not_14 (not_14_out, multiplexer_1_out[1]);
  not not_15 (not_15_out, multiplexer_1_out[2]);
  not not_16 (not_16_out, multiplexer_1_out[3]);
  not not_17 (not_17_out, multiplexer_1_out[0]);
  not not_18 (not_18_out, multiplexer_1_out[1]);
  not not_19 (not_19_out, multiplexer_1_out[3]);
  not not_20 (not_20_out, multiplexer_1_out[3]);
  not not_21 (not_21_out, multiplexer_1_out[0]);
  and and_1 (and_1_out, not_21_out, not_22_out, not_23_out);
  not not_22 (not_22_out, multiplexer_1_out[2]);
  not not_23 (not_23_out, multiplexer_1_out[3]);
  not not_24 (not_24_out, multiplexer_1_out[0]);
  not not_25 (not_25_out, multiplexer_1_out[3]);
  not not_26 (not_26_out, multiplexer_1_out[0]);
  not not_27 (not_27_out, multiplexer_1_out[1]);
  not not_28 (not_28_out, multiplexer_1_out[2]);
  or or_1 (or_1_out, and_2_out, and_3_out);
  and and_2 (and_2_out, not_1_out, not_2_out, multiplexer_1_out[2], not_3_out);
  and and_3 (and_3_out, multiplexer_1_out[0], not_4_out, not_5_out, not_6_out);
  or or_2 (or_2_out, and_4_out, and_5_out);
  not not_29 (not_29_out, or_2_out);
  and and_4 (and_4_out, not_7_out, multiplexer_1_out[1], multiplexer_1_out[2], not_8_out);
  and and_5 (and_5_out, multiplexer_1_out[0], not_9_out, multiplexer_1_out[2], not_10_out);
  not not_30 (not_30_out, and_6_out);
  and and_6 (and_6_out, not_11_out, multiplexer_1_out[1], not_12_out, not_13_out);
  and and_7 (and_7_out, multiplexer_1_out[0], not_14_out, not_15_out, not_16_out);
  not not_31 (not_31_out, or_3_out);
  or or_3 (or_3_out, and_7_out, and_8_out, and_9_out);
  and and_8 (and_8_out, not_17_out, not_18_out, multiplexer_1_out[2], not_19_out);
  and and_9 (and_9_out, multiplexer_1_out[0], multiplexer_1_out[1], multiplexer_1_out[2], not_20_out);
  or or_4 (or_4_out, and_1_out, and_10_out, and_11_out);
  and and_10 (and_10_out, not_24_out, multiplexer_1_out[1], multiplexer_1_out[2], not_25_out);
  and and_11 (and_11_out, not_26_out, not_27_out, not_28_out, multiplexer_1_out[3]);
  not not_32 (not_32_out, or_1_out);
  not not_33 (not_33_out, or_5_out);
  or or_5 (or_5_out, and_12_out, and_14_out);
  and and_12 (and_12_out, multiplexer_1_out[0], not_35_out, not_36_out, not_34_out);
  not not_34 (not_34_out, multiplexer_1_out[3]);
  not not_35 (not_35_out, multiplexer_1_out[1]);
  not not_36 (not_36_out, multiplexer_1_out[2]);
  and and_13 (and_13_out, not_38_out, not_37_out, not_42_out);
  and and_14 (and_14_out, multiplexer_1_out[1], not_39_out, not_40_out);
  not not_37 (not_37_out, multiplexer_1_out[2]);
  not not_38 (not_38_out, multiplexer_1_out[1]);
  not not_39 (not_39_out, multiplexer_1_out[2]);
  not not_40 (not_40_out, multiplexer_1_out[3]);
  not not_41 (not_41_out, or_6_out);
  or or_6 (or_6_out, and_13_out, and_15_out);
  and and_15 (and_15_out, multiplexer_1_out[0], multiplexer_1_out[1], multiplexer_1_out[2], not_43_out);
  not not_42 (not_42_out, multiplexer_1_out[3]);
  not not_43 (not_43_out, multiplexer_1_out[3]);
  _7_Segment_Display u_7_segment_display_1 (.g(n8_bit_register_1_out_5[7]));  // open: f, a, b, e, d, c, dp
  _7_Segment_Display u_7_segment_display_2 (
    .g(not_41_out), .f(not_33_out), .a(not_32_out), .b(not_29_out), .e(or_4_out), .d(not_31_out),
    .c(not_30_out));  // open: dp
endmodule

module Keypad (
  input  _7,
  input  _8,
  input  _9,
  input  _4,
  input  _5,
  input  _6,
  input  _1,
  input  _2,
  input  _3,
  input  _0,
  output [7:0] out_11
);

  wire or_1_out;
  wire [7:0] or_5_out;

  or or_1 (or_1_out, _9, _8, _7, _6, _5, _4, _3, _2, _1, _0);
  or or_2 (or_5_out[3], _9, _8);
  or or_3 (or_5_out[2], _7, _6, _5, _4);
  or or_4 (or_5_out[1], _7, _6, _2, _3);
  or or_5 (or_5_out[0], _9, _7, _5, _3, _1);
  _8_Bit_Register u_8_bit_register_1 (
    .in_4(or_5_out), .out_5(out_11), .write(or_1_out), .clock(or_1_out));  // open: Clear
endmodule

module Incrementer (
  input  [3:0] in_1,
  output [3:0] out_2
);

  wire half_adder_1_out_4, half_adder_2_out_4, half_adder_3_out_4, not_1_out, or_1_out;

  not not_1 (not_1_out, in_1[0]);
  or or_1 (or_1_out, in_1[0], not_1_out);
  Half_Adder half_adder_1 (.in_1(or_1_out), .in_2(in_1[0]), .out_3(out_2[0]), .out_4(half_adder_1_out_4));
  Half_Adder half_adder_2 (.in_1(half_adder_1_out_4), .in_2(in_1[1]), .out_3(out_2[1]), .out_4(half_adder_2_out_4));
  Half_Adder half_adder_3 (.in_1(half_adder_2_out_4), .in_2(in_1[2]), .out_3(out_2[2]), .out_4(half_adder_3_out_4));
  Half_Adder half_adder_4 (.in_1(half_adder_3_out_4), .in_2(in_1[3]), .out_3(out_2[3]));  // open: out_4
endmodule

module PC (
  input  Clear,
  input  Update,
  input  clock,
  input  [3:0] in_4,
  output [3:0] out_5
);

  _4_Bit_Register u_4_bit_register_1 (
    .Write_Value(in_4), .Read_Value(out_5), .Clear(Clear), .write(Update), .clock(clock));
endmodule

module Stage_Counter (
  input  Clock,
  input  Clear,
  output out_3,
  output out_4,
  output out_5,
  output out_6
);

  wire j_k_ff_1_q, j_k_ff_1_qn, j_k_ff_2_q, not_1_out;

  not not_1 (not_1_out, Clock);
  J_K_Flip_Flop j_k_ff_1 (
    .J(not_1_out), .clk(not_1_out), .K(not_1_out), .Q(j_k_ff_1_q), .Qn(j_k_ff_1_qn), .reset(Clear));  // open: preset, en
  and _00 (out_3, ~j_k_ff_1_q, ~j_k_ff_2_q);  // AND_Gate
  and _01 (out_4, j_k_ff_1_q, ~j_k_ff_2_q);  // AND_Gate
  J_K_Flip_Flop j_k_ff_2 (
    .J(not_1_out), .clk(j_k_ff_1_qn), .K(not_1_out), .Q(j_k_ff_2_q), .reset(Clear));  // open: Qn, preset, en
  and _03 (out_6, j_k_ff_2_q, j_k_ff_1_q);
  and _02 (out_5, j_k_ff_2_q, ~j_k_ff_1_q);  // AND_Gate

  // Notes on the sheet:
  //   Stage 00 - FETCH
  //   Stage 01 - LOAD
  //   Stage 10 - EXECUTE
  //   Stage 11 - STORE / NEXT PC
  //   This is necessary in order to make the 
  //   CPU act in a classical fashion.
endmodule

module Power_Supply (
  input  Toggle,
  input  Power_OFF,
  input  Clock,
  output Clock_Out,
  output Power_ON
);

  J_K_Flip_Flop j_k_ff_1 (.J(Power_OFF), .clk(Power_OFF), .K(Power_OFF), .Qn(Power_ON));  // open: Q, preset, en, reset
  and and_1 (Clock_Out, ~Toggle, Power_ON, Clock);  // AND_Gate
endmodule

module _4_Bit_Register (
  input  Clear,
  input  write,
  input  clock,
  input  [3:0] Write_Value,
  output [3:0] Read_Value
);

  wire and_1_out, not_1_out, not_2_out, not_3_out, not_4_out;

  and and_1 (and_1_out, write, clock);
  not not_1 (not_1_out, Write_Value[0]);
  not not_2 (not_2_out, Write_Value[1]);
  not not_3 (not_3_out, Write_Value[2]);
  not not_4 (not_4_out, Write_Value[3]);
  S_R_Flip_Flop s_r_ff_1 (
    .S(Write_Value[0]), .clk(and_1_out), .R(not_1_out), .Q(Read_Value[0]), .reset(Clear));  // open: Qn, preset, en
  S_R_Flip_Flop s_r_ff_2 (
    .S(Write_Value[1]), .clk(and_1_out), .R(not_2_out), .Q(Read_Value[1]), .reset(Clear));  // open: Qn, preset, en
  S_R_Flip_Flop s_r_ff_3 (
    .S(Write_Value[2]), .clk(and_1_out), .R(not_3_out), .Q(Read_Value[2]), .reset(Clear));  // open: Qn, preset, en
  S_R_Flip_Flop s_r_ff_4 (
    .S(Write_Value[3]), .clk(and_1_out), .R(not_4_out), .Q(Read_Value[3]), .reset(Clear));  // open: Qn, preset, en
endmodule

module Zero (
  input  [7:0] in_1,
  output out_2
);

  wire or_1_out;

  or or_1 (or_1_out, in_1[0], in_1[1], in_1[2], in_1[3], in_1[5], in_1[6], in_1[7], in_1[4]);
  not not_1 (out_2, or_1_out);
endmodule
