// Logisim project multiplication.circ as structural Verilog: 5 circuits, main circuit main
module main (
  input  in_1,
  input  in_2,
  input  in_3,
  input  in_4,
  input  in_5,
  input  in_6,
  input  in_7,
  input  in_8,
  input  in_9,
  input  in_10,
  input  in_11,
  input  in_12,
  input  in_13,
  input  in_14,
  input  in_15,
  input  in_16
);

  wire [2:0] fullencoder_1_out_9, fullencoder_1_out_10, fullencoder_1_out_11, fullencoder_1_out_12;
  wire [7:0] negator_1_out;
  wire [9:0] partialproduct_1_out_15, partialproduct_2_out_15, partialproduct_3_out_15,
       partialproduct_4_out_15;
  wire [15:0] adder_1_out, adder_2_out, adder_3_out, bit_extender_1_out, bit_extender_2_out,
       bit_extender_3_out, bit_extender_4_out, shifter_1_out, shifter_2_out, shifter_3_out;

  Negator negator_1 (.in({in_1, in_2, in_3, in_4, in_5, in_6, in_7, in_8}), .out(negator_1_out));
  fullencoder fullencoder_1 (
    .in_1(in_9), .in_2(in_10), .in_3(in_11), .in_4(in_12), .in_5(in_13), .in_6(in_14), .in_7(in_15),
    .in_8(in_16), .out_9(fullencoder_1_out_9), .out_10(fullencoder_1_out_10), .out_11(fullencoder_1_out_11),
    .out_12(fullencoder_1_out_12));
  partialproduct partialproduct_1 (
    .neg(fullencoder_1_out_9[0]), ._2x(fullencoder_1_out_9[1]), .x(fullencoder_1_out_9[2]),
    .in_1({in_1, in_2, in_3, in_4, in_5, in_6, in_7, in_8}), .in_2(negator_1_out),
    .out_6(partialproduct_1_out_15[9]), .out_7(partialproduct_1_out_15[8]),
    .out_8(partialproduct_1_out_15[7]), .out_9(partialproduct_1_out_15[6]),
    .out_10(partialproduct_1_out_15[5]), .out_11(partialproduct_1_out_15[4]),
    .out_12(partialproduct_1_out_15[3]), .out_13(partialproduct_1_out_15[2]),
    .out_14(partialproduct_1_out_15[1]), .out_15(partialproduct_1_out_15[0]));
  partialproduct partialproduct_2 (
    .neg(fullencoder_1_out_10[0]), ._2x(fullencoder_1_out_10[1]), .x(fullencoder_1_out_10[2]),
    .in_1({in_1, in_2, in_3, in_4, in_5, in_6, in_7, in_8}), .in_2(negator_1_out),
    .out_6(partialproduct_2_out_15[9]), .out_7(partialproduct_2_out_15[8]),
    .out_8(partialproduct_2_out_15[7]), .out_9(partialproduct_2_out_15[6]),
    .out_10(partialproduct_2_out_15[5]), .out_11(partialproduct_2_out_15[4]),
    .out_12(partialproduct_2_out_15[3]), .out_13(partialproduct_2_out_15[2]),
    .out_14(partialproduct_2_out_15[1]), .out_15(partialproduct_2_out_15[0]));
  partialproduct partialproduct_3 (
    .neg(fullencoder_1_out_11[0]), ._2x(fullencoder_1_out_11[1]), .x(fullencoder_1_out_11[2]),
    .in_1({in_1, in_2, in_3, in_4, in_5, in_6, in_7, in_8}), .in_2(negator_1_out),
    .out_6(partialproduct_3_out_15[9]), .out_7(partialproduct_3_out_15[8]),
    .out_8(partialproduct_3_out_15[7]), .out_9(partialproduct_3_out_15[6]),
    .out_10(partialproduct_3_out_15[5]), .out_11(partialproduct_3_out_15[4]),
    .out_12(partialproduct_3_out_15[3]), .out_13(partialproduct_3_out_15[2]),
    .out_14(partialproduct_3_out_15[1]), .out_15(partialproduct_3_out_15[0]));
  partialproduct partialproduct_4 (
    .neg(fullencoder_1_out_12[0]), ._2x(fullencoder_1_out_12[1]), .x(fullencoder_1_out_12[2]),
    .in_1({in_1, in_2, in_3, in_4, in_5, in_6, in_7, in_8}), .in_2(negator_1_out),
    .out_6(partialproduct_4_out_15[9]), .out_7(partialproduct_4_out_15[8]),
    .out_8(partialproduct_4_out_15[7]), .out_9(partialproduct_4_out_15[6]),
    .out_10(partialproduct_4_out_15[5]), .out_11(partialproduct_4_out_15[4]),
    .out_12(partialproduct_4_out_15[3]), .out_13(partialproduct_4_out_15[2]),
    .out_14(partialproduct_4_out_15[1]), .out_15(partialproduct_4_out_15[0]));
  assign bit_extender_1_out = {{6{partialproduct_1_out_15[9]}}, partialproduct_1_out_15};  // Bit_Extender bit_extender_1
  assign bit_extender_2_out = {{6{partialproduct_2_out_15[9]}}, partialproduct_2_out_15};  // Bit_Extender bit_extender_2
  assign bit_extender_3_out = {{6{partialproduct_3_out_15[9]}}, partialproduct_3_out_15};  // Bit_Extender bit_extender_3
  assign bit_extender_4_out = {{6{partialproduct_4_out_15[9]}}, partialproduct_4_out_15};  // Bit_Extender bit_extender_4
  Shifter #(.width(16)) shifter_1 (.in(bit_extender_2_out), .\dist (4'b0010), .out(shifter_1_out));
  Shifter #(.width(16)) shifter_2 (.in(bit_extender_4_out), .\dist (4'b0010), .out(shifter_2_out));
  Adder #(.width(16)) adder_1 (.a(bit_extender_1_out), .b(shifter_1_out), .out(adder_1_out));  // open: cin, cout
  Adder #(.width(16)) adder_2 (.a(bit_extender_3_out), .b(shifter_2_out), .out(adder_2_out));  // open: cin, cout
  Shifter #(.width(16)) shifter_3 (.in(adder_2_out), .\dist (4'b0100), .out(shifter_3_out));
  Adder #(.width(16)) adder_3 (.a(adder_1_out), .b(shifter_3_out), .out(adder_3_out));  // open: cin, cout
endmodule

module booth_encoder (
  input  yn_1,
  input  yn,
  input  yn_1_2,
  output x,
  output _2x,
  output neg
);

  wire xnor_1_out;

  xor xor_1 (x, yn_1, yn);
  xnor xnor_1 (xnor_1_out, yn, yn_1_2);
  nor nor_1 (_2x, x, xnor_1_out);

  assign neg = yn_1_2;
endmodule

module fullencoder (
  input  in_1,
  input  in_2,
  input  in_3,
  input  in_4,
  input  in_5,
  input  in_6,
  input  in_7,
  input  in_8,
  output [2:0] out_9,
  output [2:0] out_10,
  output [2:0] out_11,
  output [2:0] out_12
);

  booth_encoder booth_encoder_1 (.yn_1(1'b0), .yn(in_1), .yn_1_2(in_2), .x(out_9[2]), ._2x(out_9[1]), .neg(out_9[0]));
  booth_encoder booth_encoder_2 (
    .yn_1(in_2), .yn(in_3), .yn_1_2(in_4), .x(out_10[2]), ._2x(out_10[1]), .neg(out_10[0]));
  booth_encoder booth_encoder_3 (
    .yn_1(in_4), .yn(in_5), .yn_1_2(in_6), .x(out_11[2]), ._2x(out_11[1]), .neg(out_11[0]));
  booth_encoder booth_encoder_4 (
    .yn_1(in_6), .yn(in_7), .yn_1_2(in_8), .x(out_12[2]), ._2x(out_12[1]), .neg(out_12[0]));
endmodule

module partialproduct (
  input  [7:0] in_1,
  input  [7:0] in_2,
  input  neg,
  input  _2x,
  input  x,
  output out_6,
  output out_7,
  output out_8,
  output out_9,
  output out_10,
  output out_11,
  output out_12,
  output out_13,
  output out_14,
  output out_15
);

  wire and_1_out, and_2_out, and_4_out, and_5_out, and_6_out, and_7_out, and_8_out, and_9_out, and_10_out,
       and_11_out, and_12_out, and_13_out, and_14_out, and_15_out, and_16_out;
  wire [7:0] multiplexer_1_out;

  and and_1 (and_1_out, multiplexer_1_out[7], _2x);
  and and_2 (and_2_out, multiplexer_1_out[7], x);
  and and_3 (out_6, x, multiplexer_1_out[7]);
  or or_1 (out_8, and_2_out, and_4_out);
  or or_2 (out_7, and_1_out, out_6);
  and and_4 (and_4_out, multiplexer_1_out[6], _2x);
  and and_5 (and_5_out, multiplexer_1_out[6], x);
  and and_6 (and_6_out, multiplexer_1_out[5], _2x);
  or or_3 (out_9, and_5_out, and_6_out);
  Multiplexer #(.width(8)) multiplexer_1 (.in0(in_1), .in1(in_2), .out(multiplexer_1_out), .sel(neg));  // open: en
  and and_7 (and_7_out, multiplexer_1_out[4], _2x);
  and and_8 (and_8_out, multiplexer_1_out[5], x);
  or or_4 (out_10, and_8_out, and_7_out);
  and and_9 (and_9_out, multiplexer_1_out[3], _2x);
  and and_10 (and_10_out, multiplexer_1_out[4], x);
  and and_11 (and_11_out, multiplexer_1_out[3], x);
  or or_5 (out_12, and_11_out, and_13_out);
  or or_6 (out_11, and_10_out, and_9_out);
  and and_12 (and_12_out, multiplexer_1_out[1], _2x);
  and and_13 (and_13_out, multiplexer_1_out[2], _2x);
  and and_14 (and_14_out, multiplexer_1_out[2], x);
  or or_7 (out_13, and_14_out, and_12_out);
  and and_15 (and_15_out, multiplexer_1_out[1], x);
  and and_16 (and_16_out, multiplexer_1_out[0], _2x);
  or or_8 (out_14, and_15_out, and_16_out);
  and and_17 (out_15, multiplexer_1_out[0], x);
endmodule

module test (
  input  in_1,
  input  in_2,
  input  in_3,
  input  in_4,
  input  in_5,
  input  in_6,
  input  in_7,
  input  in_8,
  input  in_9,
  input  in_10,
  input  in_11,
  input  in_12,
  input  in_13,
  input  in_14,
  input  in_15,
  input  in_16
);

  wire [2:0] fullencoder_1_out_9, fullencoder_1_out_10, fullencoder_1_out_11, fullencoder_1_out_12;
  wire [7:0] multiplexer_1_out, negator_1_out;
  wire [8:0] negator_2_out, undriven;

  fullencoder fullencoder_1 (
    .in_1(in_9), .in_2(in_10), .in_3(in_11), .in_4(in_12), .in_5(in_13), .in_6(in_14), .in_7(in_15),
    .in_8(in_16), .out_9(fullencoder_1_out_9), .out_10(fullencoder_1_out_10), .out_11(fullencoder_1_out_11),
    .out_12(fullencoder_1_out_12));
  Negator negator_1 (.in({in_1, in_2, in_3, in_4, in_5, in_6, in_7, in_8}), .out(negator_1_out));
  Multiplexer #(.width(8)) multiplexer_1 (
    .in0({in_1, in_2, in_3, in_4, in_5, in_6, in_7, in_8}), .in1(negator_1_out), .out(multiplexer_1_out),
    .sel(fullencoder_1_out_9[0]));  // open: en
  // partialproduct partialproduct_1: pin names not known; wires that end beside it: fullencoder_1_out_9, fullencoder_1_out_9, multiplexer_1_out[7], undriven[8], multiplexer_1_out[6], undriven[7], undriven[6], undriven[5], undriven[4], undriven[3]
  Negator #(.width(9)) negator_2 (.in(undriven), .out(negator_2_out));
endmodule
